# Fritzing sketch PumpkinCandle (saved by Fritzing 0.7.9b)
breadboards: 1

parts:
  LED1 = LED - 5mm [color="Red (633nm)" package="5 mm [THT]"]
  LED2 = LED - 5mm [color="Yellow (592nm)" package="5 mm [THT]"]
  + = Battery
  R1 = Resistor [tolerance=±5% resistance=2.2k package=THT]
  R2 = Resistor [tolerance=±5% resistance=10k package=THT]
  R3 = Resistor [tolerance=±5% resistance=10k package=THT]
  U1 = attiny85 [package=dip]
  Q1 = LTR-3208E [part_number="Digikey 160-1031-ND"]

nets:
  N1: LED1.cathode, LED2.cathode, +.-, R3.Pin_1, U1.Pin_4, Q1.E
  N2: LED1.anode, U1.Pin_5
  N3: LED2.anode, U1.Pin_6
  N4: +.+, R2.Pin_1, U1.Pin_8
  N5: R1.Pin_0, U1.Pin_3, Q1.C
  N6: R1.Pin_1, U1.Pin_2
  N7: R2.Pin_0, U1.Pin_1
  N8: R3.Pin_0, U1.Pin_7

notes:
  PumpkinCandle 1.0
  Eric Hein 2012/10/11
  -
  collector
  emitter
  ATtiny
  25/45/85
  Red
  Yellow

custom parts:
  LTR-3208E: NPN Phototransistor 5mm IR Dark
